# Fritzing sketch Untitled Sketch 2 (saved by Fritzing 1.0.1rc)
breadboards: 1

parts:
  U1 = L298_BRIDGE_DRIVER [package=powerso20]
  R1 = Rotary Potentiometer (Small) [maximum_resistance=100kΩ knob_status=50% package=THT]
  Part1 = Arduino Leonardo (Rev3b)
  M2 = Stepper Motor - Bipolar
  BAT1 = Battery Holders [package=battery-aa-panel]

nets:
  GND: U1.GND, R1.leg2, Part1.GND, BAT1.-
  N1: U1.OUT1, M2.D
  N2: U1.OUT2, M2.C
  5V: U1.VS, U1.ENA, U1.ENB, R1.leg1, Part1.5V
  N3: U1.IN1, Part1.D8/A8
  N4: U1.IN2, Part1.D9_PWM/A9
  VCC: U1.VSS, BAT1.+
  N5: U1.IN3, Part1.D10_PWM/A10
  N6: U1.IN4, Part1.D11_PWM
  N7: U1.OUT3, M2.B
  N8: U1.OUT4, M2.A
  N9: R1.wiper, Part1.D6_PWM/A7
